# Fritzing sketch esp32-wificlock (saved by Fritzing 1.0.3b)
circuit board: 8.51138cm x 9.17657cm
breadboards: 1

parts:
  Part1 = BH1750
  ZS-042_RTC1 = ZS-042 RTC Module
  microSD1 = MicroSD Card Module
  A1 = Wemos S2 Mini [part_number="Wemos Lolin S2 mini"]
  LCD1 = GC9A01 1.28inch IPS LCD

nets:
  VCC: Part1.VCC, ZS-042_RTC1.VCC, microSD1.VCC, A1.Pin_8, LCD1.Pin_2
  GND: Part1.GND, ZS-042_RTC1.GND, microSD1.GND, A1.Pin_18, A1.Pin_26, LCD1.Pin_1
  N1: Part1.SCL, ZS-042_RTC1.SCL, A1.Pin_28
  N2: Part1.SDA, ZS-042_RTC1.SDA, A1.Pin_27
  N3: ZS-042_RTC1.SQW, A1.Pin_9
  N4: microSD1.MISO, A1.Pin_30
  N5: microSD1.MOSI, A1.Pin_29
  N6: microSD1.SCK, A1.Pin_31
  N7: microSD1.CS, A1.Pin_32
  N8: A1.Pin_10, LCD1.Pin_8
  N9: A1.Pin_11, LCD1.Pin_6
  N10: A1.Pin_12, LCD1.Pin_5
  N11: A1.Pin_13, LCD1.Pin_7
  N12: A1.Pin_14, LCD1.Pin_3
  N13: A1.Pin_16, LCD1.Pin_4

custom parts:
  BH1750: Light Sensor
  Wemos S2 Mini: A mini wifi board based on the ESP32-S2FN4R2.
  GC9A01 1.28inch IPS LCD: TFT Display 1.28 Inch TFT LCD Display Module Round RGB 240*240 GC9A01 Driver 4 Wire SPI Interface 240x240.
